# Fritzing sketch wiring diagram rtc ds1307 lcd i2c 16x2 esp8266 templet (saved by Fritzing 0.9.9b)
breadboards: 1

parts:
  U1 = NodeMCU V1.0
  Tiny_RTC1 = Tiny RTC
  Part1 = LCD1602-I2C

nets:
  N1: U1.D1, Tiny_RTC1.SCL#1
  N2: U1.D2, Tiny_RTC1.SDA#2, Part1.SDA
  VIN: U1.Vin, Tiny_RTC1.VCC#3, Part1.VCC
  N3: Tiny_RTC1.GND#4, Part1.GND

notes:
  RTC DS1307
  VCC 3.3V / Vin VCC
  GND GND GND
  SDA GPIO4 (D2) SDA
  SCL GPIO5 (D1) SCL
  LCD I2C
  VCC 3.3V / Vin VCC
  GND GND GND
  SDA GPIO4 (D2) SDA
  SCL GPIO5 (D1) SCL

custom parts:
  NodeMCU V1.0: ESP8266 based NodeMCU
  Tiny RTC: Tiny RTC I2C module DS1370Z RTC and AT24C32 EEPROM
  LCD1602-I2C: A standard character display, usually with 2x16 characters. Comes in many colors with LCM1602 IIC attached.
